# Fritzing sketch hydro (saved by Fritzing 0.9.9b)

parts:
  Part2 = Arduino Mega ADK (Rev3)
  Part3 = Ambient Light Sensor (TEMT6000 Breakout Board)
  EC_sensor = Dagu DGServo 9g header connector (female) [package=THT]
  U3 = TJA1040 [package=so08]

nets:
  N1: Part2.A0, U3.Analog
  N2: Part2.D19/RX1, EC_sensor.rx
  N3: Part2.D18/TX1, EC_sensor.tx
  5V: Part2.5V, U3.VCC
  GND: Part2.GND, EC_sensor.gnd, U3.GND#1
  N4: Part3.VCC, U3.VCC2
  N5: Part3.GND, U3.GND#0
  N6: Part3.A, U3.A

custom parts:
  Ambient Light Sensor (TEMT6000 Breakout Board): Description: Basic breakout board for the TEMT6000 Ambient Light Sensor. Only what you need, nothing you don't. Sensor acts like a transistor - the greater the incoming light, the higher the analog voltage on the signal pin. Documents: Datasheet Wiring Example
  Dagu DGServo 9g header connector (female): Dagu DGServo 9g header connector (female) This part represents the header plug found on the DGServo 9g. It is based on the standard female header, but is labelled to clearly indicate the ground, Vcc and pulse pins in schematic view. To use it, simply plug this part onto whichever header pins you are using, then attach the wires from a DGServo 9g part to the back of it. In schematic view,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
  TJA1040: CAN Tranceiver
